# Fritzing sketch ULN2003_MotorControl6Wire (saved by Fritzing 0.9.0b)
breadboards: 1

parts:
  IC1 = ULN2003A [package="SO16 [SMD]"]
  Airpax_Stepper_Motor_6Wire = Stepper Motor - Unipolar
  Part1 = Arduino Leonardo (Rev3b)
  VCC1 = Battery block 9V

nets:
  N1: IC1.In_1, Part1.D11_PWM
  N2: IC1.In_2, Part1.D10_PWM/A10
  N3: IC1.In_3, Part1.D9_PWM/A9
  N4: IC1.In_4, Part1.D8/A8
  N5: IC1.0V, Part1.GND, VCC1.-
  N6: IC1.COM_-_Common, Airpax_Stepper_Motor_6Wire.COMMON_1, Airpax_Stepper_Motor_6Wire.COMMON_2, VCC1.+
  N7: IC1.Out_4, Airpax_Stepper_Motor_6Wire.D
  N8: IC1.Out_3, Airpax_Stepper_Motor_6Wire.B
  N9: IC1.Out_2, Airpax_Stepper_Motor_6Wire.C
  N10: IC1.Out_1, Airpax_Stepper_Motor_6Wire.A
